// Logisim project 2bit_adder.circ as structural Verilog: 3 circuits, main circuit half-adder
// HA
module half_adder (
  input  Input_1,
  input  Input_2,
  output output_1,
  output carry_bit
);

  xor xor_1 (output_1, Input_1, Input_2);
  and and_1 (carry_bit, Input_1, Input_2);
endmodule

// FA
module Full_adder (
  input  carry_in,
  input  input_1,
  input  input_2,
  output output_1,
  output carry_out
);

  wire half_adder_1_carry_bit, half_adder_1_output_1, half_adder_2_carry_bit;

  half_adder half_adder_1 (
    .Input_1(input_1), .Input_2(input_2), .output_1(half_adder_1_output_1), .carry_bit(half_adder_1_carry_bit));
  half_adder half_adder_2 (
    .Input_1(carry_in), .Input_2(half_adder_1_output_1), .output_1(output_1),
    .carry_bit(half_adder_2_carry_bit));
  or or_1 (carry_out, half_adder_2_carry_bit, half_adder_1_carry_bit);
endmodule

module _2bit_adder (
  input  A_0bit,
  input  A_1bit,
  input  B_0bit,
  input  B_1bit,
  output output_0bit,
  output output_1bit,
  output carry_output
);

  wire half_adder_1_carry_bit;

  half_adder half_adder_1 (
    .Input_1(A_0bit), .Input_2(B_0bit), .output_1(output_0bit), .carry_bit(half_adder_1_carry_bit));
  Full_adder full_adder_1 (
    .carry_in(half_adder_1_carry_bit), .input_1(A_1bit), .input_2(B_1bit), .output_1(output_1bit),
    .carry_out(carry_output));
endmodule
